# Fritzing sketch Circuito Modulo Deteccion Movimiento y Proximidad (saved by Fritzing 0.9.9b)
breadboards: 1

parts:
  Componente1 = InvenSense MPU6050
  HC-SR04_Sensor_1 = HC-SR04 Ultrasonic Distance Sensor
  DFRobot_DFPlayer_Mini1 = DFRobot DFPlayer Mini [part_number=DFR0299]
  U1 = LuaNode32 / ESP32
  SP1 = SPEAKER [package=pcb_mount_speaker]
  R1 = Resistor [tolerance=±5% resistance=220 package="0603 [SMD]"]

nets:
  VCC: Componente1.VCC, U1.3V3
  GND: Componente1.GND, HC-SR04_Sensor_1.GND, DFRobot_DFPlayer_Mini1.GND-1, DFRobot_DFPlayer_Mini1.GND-2, U1.GND
  N1: Componente1.SCL, U1.D22
  N2: Componente1.SDA, U1.D21
  VCC_2: HC-SR04_Sensor_1.VCC, DFRobot_DFPlayer_Mini1.VCC, U1.Vin
  N3: HC-SR04_Sensor_1.TRIG, U1.D5
  N4: HC-SR04_Sensor_1.ECHO, U1.D18
  N5: DFRobot_DFPlayer_Mini1.RX, U1.TX2, R1.Pin_0
  N6: DFRobot_DFPlayer_Mini1.TX, U1.RX2
  N7: DFRobot_DFPlayer_Mini1.SPK_1, SP1.+
  N8: DFRobot_DFPlayer_Mini1.SPK_2, SP1.-

custom parts:
  LuaNode32 / ESP32: ESP32 based LuaNode32
